# Fritzing sketch Fritzing_project (saved by Fritzing 0.9.3b)
circuit board: 8.5cm x 5.54886cm
breadboards: 1

parts:
  Parte1 = Arduino Nano (Rev3.0)
  U1 = Optocoupler [package=THT]
  D1 = Diode [package=diode-1n4148]
  D2 = Diode [package=diode-1n4148]
  D4 = Diode [package=diode-1n4148]
  R2 = Resistor [tolerance=±5% resistance=220 package=THT]
  R3 = Resistor [tolerance=±5% resistance=330 package=THT]
  R4 = Resistor [tolerance=±5% resistance=330 package=THT]
  R5 = Resistor [tolerance=±5% resistance=1.5k package=THT]
  R7 = Resistor [tolerance=±5% resistance=1k package=THT]
  R8 = Resistor [tolerance=±5% resistance=1k package=THT]
  R9 = Resistor [tolerance=±5% resistance=1k package=THT]
  C4 = Electrolytic Capacitor [capacitance=100µF package="100 mil [THT, electrolytic]"]
  R10 = Resistor [tolerance=±5% resistance=1k package=THT]
  J1 = female pin header, 2 pins [form="♀ (female)"]
  C5 = Ceramic Capacitor [capacitance=100nF package="100 mil [THT, multilayer]"]
  R11 = Resistor [tolerance=±5% resistance=1k package=THT]
  R12 = Resistor [tolerance=±5% resistance=1M package=THT]
  R13 = Rotary Potentiometer (Large) [maximum_resistance=10kΩ package=THT]
  R14 = Resistor [tolerance=±5% resistance=27k package=THT]
  R15 = Resistor [tolerance=±5% resistance=22k package=THT]
  R16 = Resistor [tolerance=±5% resistance=22k package=THT]
  R17 = Resistor [tolerance=±5% resistance=5.6k package=THT]
  C6 = Ceramic Capacitor [capacitance=1nF package="100 mil [THT, multilayer]"]
  J2 = female pin header, 2 pins [form="♀ (female)"]
  D5 = Diode [package=diode-1n4148]
  R18 = Resistor [tolerance=±5% resistance=330 package=THT]
  R20 = Resistor [tolerance=±5% resistance=22k package=THT]
  R21 = Rotary Potentiometer (Large) [maximum_resistance=10kΩ package=THT]
  R22 = Resistor [tolerance=±5% resistance=22k package=THT]
  C7 = Ceramic Capacitor [capacitance=100nF package="100 mil [THT, multilayer]"]
  R24 = Resistor [tolerance=±5% resistance=39k package=THT]
  R25 = Resistor [tolerance=±5% resistance=100k package=THT]
  R26 = Resistor [tolerance=±5% resistance=100k package=THT]
  R27 = Resistor [tolerance=±5% resistance=5.6k package=THT]
  R28 = Resistor [tolerance=±5% resistance=47k package=THT]
  C8 = Electrolytic Capacitor [capacitance=3.3µF package="100 mil [THT, electrolytic]"]
  C9 = Electrolytic Capacitor [capacitance=3.3µF package="100 mil [THT, electrolytic]"]
  R29 = Resistor [tolerance=±5% resistance=100k package=THT]
  JP2 = Header 4 [package=screwterminal-3.5mm-4_lock]
  JP3 = Header 4 [package=screwterminal-3.5mm-4_lock]
  LED1 = LED - 5mm [color="Red (633nm)" package="5 mm [THT]"]
  LED2 = LED - 5mm [color="Red (633nm)" package="5 mm [THT]"]
  LED3 = LED - 5mm [color="Red (633nm)" package="5 mm [THT]"]
  R30 = Resistor [tolerance=±5% resistance=470 package=THT]
  R31 = Resistor [tolerance=±5% resistance=470 package=THT]
  R32 = Resistor [tolerance=±5% resistance=470 package=THT]
  J4 = female pin header, 2 pins [form="♀ (female)"]
  R33 = Resistor [tolerance=±5% resistance=470 package=THT]
  LED4 = LED - 5mm [color="Red (633nm)" package="5 mm [THT]"]
  LED5 = LED - 5mm [color="Red (633nm)" package="5 mm [THT]"]
  LED7 = LED - 5mm [color="Red (633nm)" package="5 mm [THT]"]
  R34 = Resistor [tolerance=±5% resistance=470 package=THT]
  R35 = Resistor [tolerance=±5% resistance=10k package=THT]
  R36 = Resistor [tolerance=±5% resistance=470 package=THT]
  J5 = female pin header, 2 pins [form="♀ (female)"]
  J6 = female pin header, 2 pins [form="♀ (female)"]
  C10 = Ceramic Capacitor [capacitance=100nF package="100 mil [THT, multilayer]"]
  C11 = Electrolytic Capacitor [capacitance=100µF package="100 mil [THT, electrolytic]"]
  R37 = Resistor [tolerance=±5% resistance=10k package=THT]
  R38 = Resistor [tolerance=±5% resistance=10k package=THT]
  R1 = Resistor [tolerance=±5% resistance=22k package=THT]
  D3 = Diode [package=diode-1n4148]
  C3 = Ceramic Capacitor [capacitance=2.2nF package="200 mil [THT, multilayer]"]
  C2 = Ceramic Capacitor [capacitance=2.2nF package="200 mil [THT, multilayer]"]
  Q1 = NPN-Transistor [package="TO92 [THT]"]
  Q2 = NPN-Transistor [package="TO92 [THT]"]
  C1 = Ceramic Capacitor [capacitance=2.2nF package="200 mil [THT, multilayer]"]
  IC2 = IC, DIP package, 14 pins [chip_label=IC]
  C12 = Tantalum Capacitor [capacitance=3.3µF package="200 mil [THT, tantalum]"]
  J3 = female pin header, 2 pins [form="♀ (female)"]
  R19 = Resistor [tolerance=±5% resistance=10k package=THT]
  R39 = Resistor [tolerance=±5% resistance=15k package=THT]

nets:
  N1: Parte1.D0/RX, U1.Pin_5
  GND: Parte1.GND, U1.Pin_4, R5.Pin_1, R9.Pin_1, C4.-, R10.Pin_1, J1.pin1, R13.leg1, C7.0, R29.Pin_1, LED1.cathode, LED2.cathode, LED3.cathode, J4.pin1, LED4.cathode, LED5.cathode, LED7.cathode, J6.pin1, C10.0, C11.-, IC2.pin11, J3.pin2
  N2: Parte1.D2, R32.Pin_0
  N3: Parte1.D3, R22.Pin_0
  N4: Parte1.D4, R30.Pin_0
  N5: Parte1.D5, R31.Pin_0
  N6: Parte1.D6, R33.Pin_0
  N7: Parte1.D7, R34.Pin_0
  N8: Parte1.D8, R35.Pin_1, J5.pin1
  N9: Parte1.D9, R16.Pin_0
  N10: Parte1.D10, R1.Pin_0
  N11: Parte1.D11/MOSI, J4.pin2, R38.Pin_1
  N12: Parte1.D12/MISO, J5.pin2, R37.Pin_1
  12V: Parte1.VIN, R2.Pin_0, R8.Pin_0, J1.pin2, R13.leg2, R24.Pin_1, C10.1, C11.+, IC2.pin4
  5V: Parte1.5V, R35.Pin_0, J6.pin2, R37.Pin_0, R38.Pin_0
  N13: Parte1.A7, JP3.1
  N14: Parte1.A6, JP3.2
  N15: Parte1.A5, JP3.3
  N16: Parte1.A4, JP3.4
  N17: Parte1.A3, JP2.1
  N18: Parte1.A2, JP2.2
  N19: Parte1.A1, JP2.3
  N20: Parte1.A0, JP2.4
  N21: Parte1.D13/SCK, R36.Pin_0
  N22: U1.Pin_1, D5.C, R18.Pin_0
  N23: U1.Pin_2, J2.pin2, D5.A
  N24: D1.A, R4.Pin_1, Q2.C
  N25: D1.C, D2.A, C1.1
  N26: D2.C, C5.0, D3.A, C2.1
  N27: D4.A, D3.C, C3.1
  N28: D4.C, R3.Pin_1, Q1.C
  N29: R2.Pin_1, R3.Pin_0, R4.Pin_0
  N30: R5.Pin_0, Q1.E, Q2.E
  N31: R7.Pin_0, C3.0, C1.0
  N32: R7.Pin_1, R21.leg1, R21.wiper, C8.+, IC2.pin8
  6V: R8.Pin_1, R9.Pin_0, C4.+, R11.Pin_0, R12.Pin_1, R20.Pin_1, R25.Pin_1, Q2.B, IC2.pin3, IC2.pin12
  N33: R10.Pin_0, C2.0, C12.-
  FILTER_OUT: C5.1, R12.Pin_0, IC2.pin10
  N34: R11.Pin_1, R14.Pin_1, R15.Pin_1, Q1.B
  N35: R13.wiper, R14.Pin_0
  LFO_EG2_OUT: R15.Pin_0, R26.Pin_1, IC2.pin7
  N36: R16.Pin_1, R17.Pin_0, C6.0, R1.Pin_1, IC2.pin2
  N37: R17.Pin_1, C6.1, IC2.pin1, R39.Pin_1
  N38: J2.pin1, R18.Pin_1
  N39: R20.Pin_0, IC2.pin9, R19.Pin_0
  N40: R21.leg2, R19.Pin_1
  N41: R22.Pin_1, C7.1, R24.Pin_0, IC2.pin5
  N42: R25.Pin_0, R26.Pin_0, IC2.pin6
  N43: R27.Pin_0, R28.Pin_1, IC2.pin13
  N44: R27.Pin_1, C8.-
  N45: R28.Pin_0, C9.+, IC2.pin14
  N46: C9.-, R29.Pin_0, J3.pin1
  N47: LED1.anode, R32.Pin_1
  N48: LED2.anode, R31.Pin_1
  N49: LED3.anode, R30.Pin_1
  N50: R33.Pin_1, LED4.anode
  N51: LED5.anode, R34.Pin_1
  N52: LED7.anode, R36.Pin_1
  VCO_OUT: C12.+, R39.Pin_0

notes:
  VIN 12V
  CUTOFF
  RESONANCE
  OUTPUT
  ARDUINO DIGITAL SYNTH WITH ANALOG FILTER
  Ernesto Gigliotti - 2017 - ernestogigliotti@gmail.com
  MIDI IN
  5V OUT
  ANALOG INS
